# Fritzing sketch s-5_pwm (saved by Fritzing 0.9.2b)
breadboards: 1

parts:
  IC1 = Dual Op-Amp [package=dip08]
  R1 = Resistor [tolerance=±5% resistance=220 package="1206 [SMD]"]
  R2 = Resistor [tolerance=±5% resistance=220 package="1206 [SMD]"]
  C1 = Capacitor [package=cap-pth-large]
  R4 = Resistor [tolerance=±5% resistance=220 package="1206 [SMD]"]
  R3 = Resistor [tolerance=±5% resistance=220 package="1206 [SMD]"]
  R5 = Resistor [tolerance=±5% resistance=220 package="1206 [SMD]"]
  Z1 = VARISTOR [package=0402-res]
  R6 = Resistor [tolerance=±5% resistance=220 package="1206 [SMD]"]

nets:
  N1: IC1.A_OUT, R4.Pin_1, R3.Pin_1
  N2: IC1.A_-IN, IC1.B_+IN, C1.1, R4.Pin_0
  N3: IC1.A_+IN, R1.Pin_1, R2.Pin_0, R3.Pin_0
  N4: IC1.A_V-, R2.Pin_1, C1.2, R5.Pin_0, Z1.2, R6.Pin_1
  N5: IC1.B_-IN, R5.Pin_1, Z1.1
  N6: IC1.B_OUT, R6.Pin_0
  N7: IC1.A_V+, R1.Pin_0
